# Fritzing sketch Bottom (saved by Fritzing 0.9.3b)
circuit board: 8.53488cm x 5.63626cm
breadboards: 1

parts:
  Raspberry_Pi_1 = Raspberry Pi 3 [part_number=RPI-3-V1.2]
  VCC1 = Screw terminal - 2 pins [package=THT]
  CHG1 = Screw terminal - 2 pins [package=THT]
  Motor = screw terminal, 4 pins
  TO_TOP = DB25F
  S_HIVOLT = Toggle Switch [package=THT]
  U1 = Voltage Regulator - 5V [package="TO220 [THT]"]
  S_CPU = Toggle Switch [package=THT]
  S_MOTOR = Toggle Switch [package=THT]
  S_LOVOLT = Toggle Switch [package=THT]
  LED_CPU = LED - 5mm [color="Red (633nm)" package="5 mm [THT]"]
  LED_MOTOR = LED - 5mm [color="Red (633nm)" package="5 mm [THT]"]
  R1 = Resistor [tolerance=±5% resistance=220 package=THT]
  IC1 = H-Bridge [package=THT]
  USB1 = USB connector [package=THT]
  TRS1 = Audio Jack (TRS) 3.5mm [package="4Ucon 08780 [THT]"]
  CONN1 = shrouded pin header, 6 pins [form="♂ (shrouded male)"]
  CONN2 = shrouded pin header, 6 pins [form="♂ (shrouded male)"]
  C2 = Ceramic Capacitor [capacitance=10µF voltage=50V package="100 mil [THT, multilayer]"]
  C1 = Ceramic Capacitor [capacitance=10µF voltage=50V package="100 mil [THT, multilayer]"]

nets:
  N1: Raspberry_Pi_1.3v3, TO_TOP.pin15, CONN1.pin5, CONN2.pin5
  N2: Raspberry_Pi_1.GPIO2, TO_TOP.pin4, CONN1.pin4, CONN2.pin4
  N3: Raspberry_Pi_1.GPIO3, TO_TOP.pin5, CONN1.pin3, CONN2.pin3
  N4: Raspberry_Pi_1.GPIO4, IC1.1_2EN
  GND: Raspberry_Pi_1.GND, VCC1.pin2, CHG1.pin2, U1.GND, R1.Pin_1, IC1.GND1, IC1.GND2, IC1.GND3, IC1.GND4, C2.0, C1.1
  N5: Raspberry_Pi_1.GPIO17, TO_TOP.pin2
  N6: Raspberry_Pi_1.GPIO5, IC1.3_4EN
  N7: Raspberry_Pi_1.GPIO6, IC1.1A
  N8: Raspberry_Pi_1.GPIO13, IC1.3A
  N9: Raspberry_Pi_1.GPIO16, IC1.4A
  N10: Raspberry_Pi_1.GPIO12, IC1.2A
  N11: Raspberry_Pi_1.GPIO18, TO_TOP.pin3
  5V: Raspberry_Pi_1.5V, TO_TOP.pin14, S_CPU.L1, LED_CPU.anode, USB1.5V
  N12: VCC1.pin1, CHG1.pin1, S_HIVOLT.COM, S_HIVOLT.L2
  N13: Motor.pin1, IC1.1Y
  N14: Motor.pin2, IC1.2Y
  N15: Motor.pin3, IC1.3Y
  N16: Motor.pin4, IC1.4Y
  N17: TO_TOP.pin1, USB1.GND, USB1.chassis6, TRS1.Sleeve, CONN1.pin1, CONN2.pin1
  N18: TO_TOP.pin6, USB1.d+
  N19: TO_TOP.pin7, USB1.d-
  N20: TO_TOP.pin8, TRS1.Ring
  N21: TO_TOP.pin9, TRS1.Tip
  N22: TO_TOP.pin16, S_HIVOLT.L1, U1.input_voltage, S_LOVOLT.COM, S_LOVOLT.L2, IC1.VCC2, CONN1.pin2, CONN2.pin2, C1.0
  N23: U1.output_voltage, C2.1
  N24: S_CPU.COM, S_CPU.L2, S_MOTOR.COM, S_MOTOR.L2, S_LOVOLT.L1, CONN1.pin6, CONN2.pin6
  N25: S_MOTOR.L1, LED_MOTOR.anode, IC1.VCC1
  N26: LED_CPU.cathode, LED_MOTOR.cathode, R1.Pin_0

notes:
  + -
  - +
  1Y 2Y 3Y 4Y
  EN1,2=4 EN3,4=5
  1A=6 2A=12 3A=13 4A=16
  SERVOS: HOR=17 VER=18
  Bottom Robot
  Circuit V.0
