# Fritzing sketch 7805 Assembly (saved by Fritzing 0.9.3b)
circuit board: 1.84322cm x 3.47086cm
breadboards: 1

parts:
  U1 = Voltage Regulator - 5V [package="TO220 [THT]"]
  U2 = Voltage Regulator - 5V [package="TO220 [THT]"]
  U3 = Voltage Regulator - 5V [package="TO220 [THT]"]
  J1 = male pin header, 3 pins [form="♂ (male)"]
  U4 = Voltage Regulator - 5V [package="TO220 [THT]"]

nets:
  N1: U1.input_voltage, U2.input_voltage, U3.input_voltage, J1.pin1, U4.input_voltage
  GND: U1.GND, U2.GND, U3.GND, J1.pin2, U4.GND
  N2: U1.output_voltage, U2.output_voltage, U3.output_voltage, J1.pin3, U4.output_voltage

notes:
  7805 Assembly V.0
