# Fritzing sketch RTC (saved by Fritzing 0.9.3b)
circuit board: 5.26106cm x 2.21583cm
breadboards: 1

parts:
  XTAL1 = Crystal [frequency="32 MHz" package=THT]
  BAT1 = Battery Holders [package=battcom_20mm_pth]
  IC1 = DS1307 [package=THT]
  C1 = Ceramic Capacitor [capacitance=10pF voltage=10V package="100 mil [THT, multilayer]"]
  C2 = Ceramic Capacitor [capacitance=10pF voltage=10V package="100 mil [THT, multilayer]"]
  CONN1 = prefix0000 [form="♂ (shrouded male)"]

nets:
  N1: XTAL1.pin_0, IC1.X2_-_Crystal, C1.1
  N2: XTAL1.pin_1, IC1.X1_-_Crystal, C2.0
  N3: BAT1.+, IC1.Vbat_-_Backup_Supply
  N4: BAT1.-, IC1.0V, C1.0, C2.1, CONN1.connector0
  N5: IC1.SDA_-_I2C_Data, CONN1.connector3
  N6: IC1.SCL_-_I2C_Clock, CONN1.connector2
  N7: IC1.+V, CONN1.connector5

notes:
  0V SCL SDA 5V 5V SDA SCL 0V
  Circuit V.0
  Bottom Robot
  RTC Module V.0
