# Fritzing sketch Top (saved by Fritzing 0.9.3b)
circuit board: 7.23695cm x 8.88573cm
breadboards: 1

parts:
  TO_BOTTOM = DB25M
  USB1 = USB Connectors [package=usb-a-s-nosilk]
  J = double row male pin header, 4 pins [form="♂ (male)"]
  TRS1 = Audio Jack (TRS) 3.5mm [package="4Ucon 08780 [THT]"]
  J_HOR = Basic Servo
  J_VER = Basic Servo
  CONN1 = shrouded pin header, 6 pins [form="♂ (shrouded male)"]
  J1 = female pin header, 2 pins [form="♀ (female)"]
  R1 = Resistor [tolerance=±5% resistance=220 package=THT]
  7_Segment1 = 7 Segment Display
  U1 = atmega328 [package=dip]

nets:
  GND: TO_BOTTOM.pin1, J_HOR.gnd, J_VER.gnd, CONN1.pin1, J1.pin1, R1.Pin_0
  N1: TO_BOTTOM.pin2, J_HOR.pulse
  N2: TO_BOTTOM.pin3, J_VER.pulse
  N3: TO_BOTTOM.pin4, CONN1.pin4, U1.A4
  N4: TO_BOTTOM.pin5, CONN1.pin3, U1.A5
  N5: TO_BOTTOM.pin6, J.pin1
  N6: TO_BOTTOM.pin7, J.pin4
  N7: TO_BOTTOM.pin8, TRS1.Ring
  N8: TO_BOTTOM.pin9, TRS1.Tip
  VCC: TO_BOTTOM.pin14, USB1.VBUS, J_HOR.vcc, J_VER.vcc, CONN1.pin6
  N9: TO_BOTTOM.pin15, CONN1.pin5, U1.VCC
  N10: USB1.D+, J.pin3
  N11: USB1.D-, J.pin2
  GND_2: USB1.GND, TRS1.Sleeve, U1.GND
  N12: J1.pin2, R1.Pin_1, 7_Segment1.common_cathode
  N13: 7_Segment1.Segment_E, U1.D6_(PWM)
  N14: 7_Segment1.Segment_D, U1.D5_(PWM)
  N15: 7_Segment1.Segment_C, U1.D4
  N16: 7_Segment1.Segment_DP, U1.D9_(PWM)
  N17: 7_Segment1.Segment_B, U1.D3_(PWM)
  N18: 7_Segment1.Segment_A, U1.D2
  N19: 7_Segment1.Segment_F, U1.D7
  N20: 7_Segment1.Segment_G, U1.D8

notes:
  D+   D-
  Circuit V.0
  Top Robot
  0V 5V
  NC 3V3
  SCL SDA
